# Fritzing sketch theWashingHandsSoundsGoodSoapDispenser (saved by Fritzing 0.9.3b)

parts:
  Part1 = Arduino Uno (Rev3)
  J1 = Piezo Speaker
  R1 = Resistor [tolerance=±5% resistance=220 package=THT]
  S1 = Pushbutton [package="[SMD]"]

nets:
  N1: Part1.D12/MISO, R1.Pin_1, S1.Pin_3, S1.Pin_4
  N2: Part1.GND, J1.pin1, R1.Pin_0
  N3: Part1.D3_PWM, J1.pin2
  N4: Part1.5V, S1.Pin_1, S1.Pin_2

// code stored in the sketch: washYourHandsSinging.ino

